# Fritzing sketch Arduino-Charlieplexing (saved by Fritzing 0.9.4)

parts:
  LED1 = LED - 5mm [color="White (4500K)" package="5 mm [THT]"]
  LED2 = LED - 5mm [color="White (4500K)" package="5 mm [THT]"]
  LED3 = LED - 5mm [color="White (4500K)" package="5 mm [THT]"]
  LED4 = LED - 5mm [color="White (4500K)" package="5 mm [THT]"]
  LED5 = LED - 5mm [color="White (4500K)" package="5 mm [THT]"]
  LED6 = LED - 5mm [color="White (4500K)" package="5 mm [THT]"]
  LED7 = LED - 5mm [color="White (4500K)" package="5 mm [THT]"]
  LED8 = LED - 5mm [color="White (4500K)" package="5 mm [THT]"]
  LED9 = LED - 5mm [color="White (4500K)" package="5 mm [THT]"]
  LED10 = LED - 5mm [color="White (4500K)" package="5 mm [THT]"]
  LED11 = LED - 5mm [color="White (4500K)" package="5 mm [THT]"]
  LED12 = LED - 5mm [color="White (4500K)" package="5 mm [THT]"]
  LED13 = LED - 5mm [color="White (4500K)" package="5 mm [THT]"]
  LED14 = LED - 5mm [color="White (4500K)" package="5 mm [THT]"]
  LED15 = LED - 5mm [color="White (4500K)" package="5 mm [THT]"]
  LED16 = LED - 5mm [color="White (4500K)" package="5 mm [THT]"]
  LED18 = LED - 5mm [color="White (4500K)" package="5 mm [THT]"]
  LED20 = LED - 5mm [color="White (4500K)" package="5 mm [THT]"]
  LED21 = LED - 5mm [color="White (4500K)" package="5 mm [THT]"]
  LED24 = LED - 5mm [color="White (4500K)" package="5 mm [THT]"]
  R1 = Resistor [tolerance=±5% resistance=220 package=THT]
  R2 = Resistor [tolerance=±5% resistance=220 package=THT]
  R3 = Resistor [tolerance=±5% resistance=220 package=THT]
  R4 = Resistor [tolerance=±5% resistance=220 package=THT]
  R5 = Resistor [tolerance=±5% resistance=220 package=THT]

nets:
  N1: LED1.cathode, LED5.anode, LED6.anode, LED7.anode, LED8.anode, LED10.cathode, LED13.cathode, LED20.cathode, R2.Pin_0
  N2: LED1.anode, LED2.anode, LED3.anode, LED4.anode, LED8.cathode, LED11.cathode, LED12.cathode, LED18.cathode, R1.Pin_0
  N3: LED2.cathode, LED6.cathode, LED9.anode, LED11.anode, LED13.anode, LED15.cathode, LED16.anode, LED24.cathode, R3.Pin_0
  N4: LED3.cathode, LED7.cathode, LED10.anode, LED12.anode, LED14.anode, LED15.anode, LED16.cathode, LED21.cathode, R4.Pin_0
  N5: LED4.cathode, LED5.cathode, LED9.cathode, LED14.cathode, LED18.anode, LED20.anode, LED21.anode, LED24.anode, R5.Pin_0

notes:
  Pin 1
  Pin 2
  Pin 3
  Pin 4
  Pin 5
